# Fritzing sketch PiTime Circuit Diagram (saved by Fritzing 0.9.3b)
breadboards: 1

parts:
  S1 = Square Pushbutton
  S2 = Square Pushbutton
  S3 = Square Pushbutton
  S4 = Square Pushbutton
  Raspberry_Pi_1 = Raspberry Pi 3 [part_number=RPI-3-V1.2]  # not connected
  Part2 = Adafruit T-Cobbler Plus [part_number="Adafruit #1989 and #2028"]
  R1 = Resistor [tolerance=±5% resistance=220 package=THT]
  R2 = Resistor [tolerance=±5% resistance=220 package=THT]
  R3 = Resistor [tolerance=±5% resistance=220 package=THT]
  R4 = Resistor [tolerance=±5% resistance=220 package=THT]

nets:
  N1: S1.leg0, R3.Pin_1
  N2: S1.leg1, Part2.SCLK
  N3: S2.leg0, R4.Pin_1
  N4: S2.leg1, Part2.GPIO22
  N5: S3.leg0, Part2.GPIO20
  N6: S3.leg1, R2.Pin_0
  N7: S4.leg0, Part2.EECLK
  N8: S4.leg1, R1.Pin_1
  N9: R1.Pin_0, R2.Pin_1
  N10: R3.Pin_0, R4.Pin_0

custom parts:
  Adafruit T-Cobbler Plus: The Raspberry Pi has landed on the Maker World like a 40-GPIO pinned, quad-USB ported, credit card sized bomb of DIY joy. And while you can use most of our great Model B accessories by hooking up our downgrade cable, its probably a good time to upgrade your set up and accessorize using all of the 40 pins. That's why we now carry the Assembled Adafruit Pi T-Cobbler Plus - Breakout + Cable for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
